# Fritzing sketch Third Eye (saved by Fritzing 0.9.0b)
breadboards: 1

parts:
  part = Blend Micro v1.0
  SONAR1 = Maxbotix MaxSonar Ultrasonic Sensor (Hi-Res)
  U1 = Voltage Regulator - 3.3V [package="TO220 [THT]"]
  C2 = Electrolytic Capacitor [capacitance=10µF voltage=50V package="1010 [SMD, electrolytic]"]
  C1 = Electrolytic Capacitor [capacitance=22µF voltage=50V package="1010 [SMD, electrolytic]"]

nets:
  N1: part.VIN, U1.output_voltage, C2.+
  N2: part.D9/PWM/A9, SONAR1.PW
  N3: part.V33, SONAR1.+5V
  GND: part.GND#34, SONAR1.GND, U1.GND, C2.-, C1.-
  Power Source: U1.input_voltage, C1.+

custom parts:
  Blend Micro v1.0: Blend Micro is a RedBearLab Arduino at Heart integrated development board, they have "blend"ed Arduino with Bluetooth 4.0 Low Energy (aka BLE or Bluetooth Smart) into a single board. It is targeted for makers to develop low power Internet-Of-Things (IoT) projects quickly and easily. The micro-controller unit (MCU) is Atmel ATmega32u4 and the BLE chip is Nordic nRF8001. Blend Micro runs as BLE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
  Maxbotix MaxSonar Ultrasonic Sensor (Hi-Res): Maxbotix MaxSonar Hi-Resolution Ultrasonic Sensor HRLV-EZ0, HRLV-EZ1, HRLV-EZ2, HRLV-EZ3, HRLV-EZ4
